// Logisim project CPU.circ as structural Verilog: 6 circuits, main circuit main
module main (
  input  [31:0] A,
  input  [31:0] B,
  input  in_3,
  input  in_4
);

  ALU alu_1 ();  // open: Reg_A_7969c0f7, Reg_B_c40337f3, Shift_by_40dae865, isLsr, isSub, isAsr, isCmp, isOr, isMul, isNot, isDiv, isAnd, isMod, EB, isLsl, isMov, isAdd, Flag_out_70c782f8, Dout
endmodule

module ControlUnit (
  input  [31:0] Instruction,
  output IsImmediate,
  output [12:0] AluSignals,
  output IsLd,
  output IsSt,
  output IsBeq,
  output IsBgt,
  output IsCall,
  output IsRet,
  output IsWb,
  output IsUbranch
);

  wire and_1_out, and_2_out, and_3_out, and_4_out, demultiplexer_1_out0, demultiplexer_1_out18, nor_1_out,
       not_1_out, not_2_out, not_3_out, not_4_out, not_5_out, or_1_out, or_2_out;

  Demultiplexer #(.enable("true"), .select(5)) demultiplexer_1 (
    .out0(demultiplexer_1_out0), .out1(AluSignals[1]), .out2(AluSignals[2]), .out3(AluSignals[3]),
    .out4(AluSignals[4]), .out5(AluSignals[5]), .out6(AluSignals[6]), .out7(AluSignals[7]),
    .out8(AluSignals[8]), .out9(AluSignals[9]), .out10(AluSignals[10]), .out11(AluSignals[11]),
    .out12(AluSignals[12]), .out14(IsLd), .out15(IsSt), .out16(IsBeq), .out17(IsBgt),
    .out18(demultiplexer_1_out18), .out19(IsCall), .out20(IsRet), .in(1'b1), .sel(Instruction[31:27]));  // open: out13, out21, out22, out23, out24, out25, out26, out27, out28, out29, out30, out31, en
  not not_1 (not_1_out, Instruction[27]);
  not not_2 (not_2_out, Instruction[28]);
  not not_3 (not_3_out, Instruction[29]);
  not not_4 (not_4_out, Instruction[30]);
  not not_5 (not_5_out, Instruction[31]);
  and and_1 (and_1_out, not_5_out, Instruction[30], Instruction[29], Instruction[28]);
  or or_1 (or_1_out, not_2_out, Instruction[30]);
  and and_2 (and_2_out, not_1_out, not_2_out, Instruction[29]);
  and and_3 (and_3_out, Instruction[28], not_3_out);
  or or_2 (or_2_out, and_2_out, and_3_out);
  or or_3 (AluSignals[0], demultiplexer_1_out0, and_1_out);
  and and_4 (and_4_out, Instruction[27], or_1_out, Instruction[29], not_5_out);
  nor nor_1 (nor_1_out, and_4_out, Instruction[31]);
  or or_4 (IsWb, IsCall, nor_1_out);
  and and_5 (IsUbranch, or_2_out, not_4_out, Instruction[31]);

  assign IsImmediate = Instruction[26];

  // Notes on the sheet:
  //   IsImmediate
  //   Is Add
  //   IsSub
  //   IsMul
  //   IsDiv
  //   IsMod
  //   IsCmp
  //   IsAnd
  //   IsOr
  //   IsNot
  //   IsMov
  //   IsLsl
  //   IsLsr
  //   IsAsr
  //   IsLd
  //   IsSt
  //   IsBeq
  //   IsBgt
  //   IsCall
  //   IsRet
  //   Is Add
  //   IsWb
  //   IsUbranch
endmodule

module ALU (
  input  isAdd,
  input  isSub,
  input  isCmp,
  input  isMul,
  input  isDiv,
  input  isMod,
  input  isLsl,
  input  isLsr,
  input  isAsr,
  input  isOr,
  input  isNot,
  input  isAnd,
  input  isMov,
  input  [31:0] Reg_A_7969c0f7,
  input  [31:0] Reg_B_c40337f3,
  input  EB,
  input  [4:0] Shift_by_40dae865,
  output [31:0] Dout,
  output [2:0] Flag_out_70c782f8
);

  wire adder_1_cout, comparator_1_eq, comparator_1_gt, comparator_1_lt, subtractor_1_bout;
  wire [4:0] Choose;
  wire [31:0] adder_1_out, and_1_out, divider_1_out, divider_1_rem, multiplier_1_out, not_1_out, or_1_out,
       shifter_1_out, shifter_2_out, shifter_3_out, subtractor_1_out;

  assign or_1_out = Reg_A_7969c0f7 | Reg_B_c40337f3;  // OR_Gate or_1, 32 bits wide
  assign not_1_out = ~Reg_A_7969c0f7;  // NOT_Gate not_1, 32 bits wide
  assign and_1_out = Reg_A_7969c0f7 & Reg_B_c40337f3;  // AND_Gate and_1, 32 bits wide
  Adder #(.width(32)) adder_1 (
    .a(Reg_A_7969c0f7), .b(Reg_B_c40337f3), .out(adder_1_out), .cout(adder_1_cout));  // open: cin
  assign Flag_out_70c782f8[0] = isAdd ? adder_1_cout : 1'bz;  // Controlled_Buffer controlled_buffer_1
  Subtractor #(.width(32)) subtractor_1 (
    .a(Reg_A_7969c0f7), .b(Reg_B_c40337f3), .out(subtractor_1_out), .bout(subtractor_1_bout));  // open: bin
  assign Flag_out_70c782f8[2] = isSub ? subtractor_1_bout : 1'bz;  // Controlled_Buffer controlled_buffer_2
  assign Flag_out_70c782f8[0] = isCmp ? comparator_1_gt : 1'bz;  // Controlled_Buffer controlled_buffer_3
  assign Flag_out_70c782f8[1] = isCmp ? comparator_1_eq : 1'bz;  // Controlled_Buffer controlled_buffer_4
  Comparator #(.width(32)) comparator_1 (
    .a(Reg_A_7969c0f7), .b(Reg_B_c40337f3), .gt(comparator_1_gt), .eq(comparator_1_eq), .lt(comparator_1_lt));
  assign Flag_out_70c782f8[2] = isCmp ? comparator_1_lt : 1'bz;  // Controlled_Buffer controlled_buffer_5
  Multiplier #(.width(32)) multiplier_1 (
    .a(Reg_A_7969c0f7), .b(Reg_B_c40337f3), .out(multiplier_1_out));  // open: cin, cout
  Divider #(.width(32)) divider_1 (
    .a(Reg_A_7969c0f7), .b(Reg_B_c40337f3), .out(divider_1_out), .rem(divider_1_rem));  // open: upper
  Shifter #(.width(32)) shifter_1 (.in(Reg_A_7969c0f7), .\dist (Shift_by_40dae865), .out(shifter_1_out));
  Shifter #(.shift("lr"), .width(32)) shifter_2 (.in(Reg_A_7969c0f7), .\dist (Shift_by_40dae865), .out(shifter_2_out));
  Shifter #(.shift("ar"), .width(32)) shifter_3 (.in(Reg_A_7969c0f7), .\dist (Shift_by_40dae865), .out(shifter_3_out));
  assign Choose = isAdd ? {5{1'b0}} : 5'bz;  // Controlled_Buffer controlled_buffer_6
  assign Choose = isSub ? 5'b00001 : 5'bz;  // Controlled_Buffer controlled_buffer_7
  assign Choose = isCmp ? 5'b00010 : 5'bz;  // Controlled_Buffer controlled_buffer_8
  assign Choose = isMul ? 5'b00011 : 5'bz;  // Controlled_Buffer controlled_buffer_9
  assign Choose = isDiv ? 5'b00100 : 5'bz;  // Controlled_Buffer controlled_buffer_10
  assign Choose = isMod ? 5'b00101 : 5'bz;  // Controlled_Buffer controlled_buffer_11
  assign Choose = isLsl ? 5'b00110 : 5'bz;  // Controlled_Buffer controlled_buffer_12
  assign Choose = isLsr ? 5'b00111 : 5'bz;  // Controlled_Buffer controlled_buffer_13
  assign Choose = isAsr ? 5'b01000 : 5'bz;  // Controlled_Buffer controlled_buffer_14
  assign Choose = isOr ? 5'b01001 : 5'bz;  // Controlled_Buffer controlled_buffer_15
  assign Choose = isNot ? 5'b01010 : 5'bz;  // Controlled_Buffer controlled_buffer_16
  assign Choose = isAnd ? 5'b01011 : 5'bz;  // Controlled_Buffer controlled_buffer_17
  assign Choose = isMov ? 5'b01100 : 5'bz;  // Controlled_Buffer controlled_buffer_18
  Multiplexer #(.enable("true"), .select(5), .width(32)) multiplexer_1 (
    .in0(adder_1_out), .in1(subtractor_1_out), .in3(multiplier_1_out), .in4(divider_1_out),
    .in5(divider_1_rem), .in6(shifter_1_out), .in7(shifter_2_out), .in8(shifter_3_out), .in9(or_1_out),
    .in10(not_1_out), .in11(and_1_out), .in12(Reg_A_7969c0f7), .out(Dout), .sel(Choose), .en(EB));  // open: in2, in13, in14, in15, in16, in17, in18, in19, in20, in21, in22, in23, in24, in25, in26, in27, in28, in29, in30, in31
  // Probe on Choose
  assign Flag_out_70c782f8[1] = isAdd ? 1'b0 : 1'bz;  // Controlled_Buffer controlled_buffer_19
  assign Flag_out_70c782f8[2] = isAdd ? 1'b0 : 1'bz;  // Controlled_Buffer controlled_buffer_20
  assign Flag_out_70c782f8[0] = isSub ? 1'b0 : 1'bz;  // Controlled_Buffer controlled_buffer_21
  assign Flag_out_70c782f8[1] = isSub ? 1'b0 : 1'bz;  // Controlled_Buffer controlled_buffer_22

  // Other names for the same wires on the sheet: add = isAdd; And = isAnd; Asr = isAsr; cmp = isCmp; div = isDiv;
  //   C = Flag_out_70c782f8[0]; Z = Flag_out_70c782f8[1]; N = Flag_out_70c782f8[2]; Lsl = isLsl; Lsr = isLsr;
  //   mod = isMod; mov = isMov; mul = isMul; Not = isNot; Or = isOr; sub = isSub
endmodule

module InstructionFetch (
  input  IsBranchTaken,
  input  [31:0] BranchPC,
  output [31:0] Instruction
);

  wire clock, reset, undriven;
  wire [31:0] adder_1_out, multiplexer_1_out, PC_q;

  Register #(.trigger("falling"), .width(32)) PC (.D(multiplexer_1_out), .en(1'b1), .clk(clock), .Q(PC_q), .clr(reset));
  Multiplexer #(.width(32)) multiplexer_1 (.in0(adder_1_out), .in1(BranchPC), .out(multiplexer_1_out), .sel(undriven));
  Adder #(.width(32)) adder_1 (.a(32'h4), .b(PC_q), .out(adder_1_out));  // open: cin, cout
  ROM #(.addrWidth(16), .dataWidth(32)) Instruction_Memory_0469d480 (.addr(PC_q[31:16]), .data(Instruction));

  // Notes on the sheet:
  //   contents of Instruction_Memory_0469d480 (hex, n*v repeats v):
  //   4c00000a 98000002 90000000 2c000001 88000003 4c400001 a0000000 fb80008 7c380000 7ff80004 c000001
  //   9ffffff8 77f80004 74380000 7b80008 10404000 a0000000
endmodule

module OperandFetch (
  output [31:0] Immx
);

  wire IsRet, IsSt;
  wire [3:0] A1, A2;
  wire [26:0] Instruction;
  wire [31:0] bit_extender_1_out, bit_extender_2_out, bit_extender_3_out, BranchTarget, multiplexer_3_out,
       PC, shifter_1_out, shifter_2_out;

  assign bit_extender_1_out = {{5{Instruction[26]}}, Instruction};  // Bit_Extender bit_extender_1
  assign bit_extender_2_out = {{16{Instruction[16]}}, Instruction[16:1]};  // Bit_Extender bit_extender_2
  assign bit_extender_3_out = {{16{1'b0}}, Instruction[16:1]};  // Bit_Extender bit_extender_3
  Shifter #(.width(32)) shifter_1 (.in(bit_extender_1_out), .\dist (5'b00010), .out(shifter_1_out));
  Adder #(.width(32)) adder_1 (.a(shifter_1_out), .b(PC), .out(BranchTarget));  // open: cin, cout
  Multiplexer #(.width(4)) multiplexer_1 (.in0(Instruction[21:18]), .in1(4'b1111), .out(A1), .sel(IsRet));
  Multiplexer #(.width(4)) multiplexer_2 (.in0(Instruction[25:22]), .in1(Instruction[17:14]), .out(A2), .sel(IsSt));
  Shifter #(.width(32)) shifter_2 (.in(bit_extender_3_out), .\dist (5'b10000), .out(shifter_2_out));
  Multiplexer #(.select(2), .width(32)) multiplexer_3 (
    .in0(bit_extender_2_out), .in1(bit_extender_3_out), .in2(shifter_2_out), .out(multiplexer_3_out),
    .sel(Instruction[18:17]));  // open: in3

  // Notes on the sheet:
  //   Register input 1
  //   Register input 2
endmodule

module ExecuteUnit (
);

  wire and_1_out, and_2_out, BranchPC, BranchTarget, IsBeq, IsBgt, IsBranchTaken, IsRet, IsUbranch,
       nor_1_out, op1;
  wire [2:1] Flag_out_70c782f8;

  and and_1 (and_1_out, IsBeq, Flag_out_70c782f8[1]);
  nor nor_1 (nor_1_out, Flag_out_70c782f8[2], Flag_out_70c782f8[1]);
  Multiplexer multiplexer_1 (.in0(BranchTarget), .in1(op1), .out(BranchPC), .sel(IsRet));
  and and_2 (and_2_out, IsBgt, nor_1_out);
  or or_1 (IsBranchTaken, IsUbranch, and_1_out, and_2_out);

  // Notes on the sheet:
  //   Flag.E
  //   Flag.GT
endmodule
